// Logisim project batalha_naval_4x4_ruan_john.circ as structural Verilog: 8 circuits, main circuit codificador
module main (
  input  N1_3,
  input  N1_2,
  input  N1_1,
  input  N1_0,
  input  N2_3,
  input  N2_2,
  input  N2_1,
  input  N2_0,
  input  l1,
  input  l0,
  input  c1,
  input  c0,
  input  disparar
);

  wire codificador_1_alvo_0, codificador_1_alvo_1, codificador_1_alvo_2, codificador_1_alvo_3,
       coluna_1_coluna_0_out, coluna_1_coluna_1_out, comparador_1_s, linha_1_linha_0_out,
       linha_1_linha_1_out, navio_1_1_n1_0_out, navio_1_1_n1_1_out, navio_1_1_n1_2_out, navio_1_1_n1_3_out,
       navio_2_1_n2_0_out, navio_2_1_n2_1_out, navio_2_1_n2_2_out, navio_2_1_n2_3_out, resultado_1_acertou,
       resultado_1_errou;

  Linha linha_1 (
    .Linha_0_in(l0), .linha_1_in(l1), .linha_0_out(linha_1_linha_0_out), .linha_1_out(linha_1_linha_1_out));
  coluna coluna_1 (
    .coluna_0_in(c0), .coluna_1_in(c1), .coluna_0_out(coluna_1_coluna_0_out),
    .coluna_1_out(coluna_1_coluna_1_out));
  navio_1 navio_1_1 (
    .N1_0_in(N1_0), .N1_1_in(N1_1), .N1_2_in(N1_2), .N1_3_in(N1_3), .N1_0_out(navio_1_1_n1_0_out),
    .N1_1_out(navio_1_1_n1_1_out), .N1_2_out(navio_1_1_n1_2_out), .N1_3_out(navio_1_1_n1_3_out));
  navio_2 navio_2_1 (
    .N2_0_in(N2_0), .N2_1_in(N2_1), .N2_2_in(N2_2), .N2_3_in(N2_3), .N2_0_out(navio_2_1_n2_0_out),
    .N2_1_out(navio_2_1_n2_1_out), .N2_2_out(navio_2_1_n2_2_out), .N2_3_out(navio_2_1_n2_3_out));
  codificador codificador_1 (
    .linha_1(linha_1_linha_1_out), .linha_0(linha_1_linha_0_out), .coluna_1(coluna_1_coluna_1_out),
    .coluna_0(coluna_1_coluna_0_out), .alvo_3(codificador_1_alvo_3), .alvo_2(codificador_1_alvo_2),
    .alvo_1(codificador_1_alvo_1), .alvo_0(codificador_1_alvo_0));
  comparador comparador_1 (
    .N1_0(navio_1_1_n1_0_out), .N1_1(navio_1_1_n1_1_out), .N1_2(navio_1_1_n1_2_out),
    .N1_3(navio_1_1_n1_3_out), .alvo_0(codificador_1_alvo_0), .alvo_1(codificador_1_alvo_1),
    .alvo_2(codificador_1_alvo_2), .alvo_3(codificador_1_alvo_3), .N2_0(navio_2_1_n2_0_out),
    .N2_1(navio_2_1_n2_1_out), .N2_2(navio_2_1_n2_2_out), .N2_3(navio_2_1_n2_3_out), .S(comparador_1_s));
  resultado resultado_1 (
    .comparador(comparador_1_s), .disparar(disparar), .acertou(resultado_1_acertou), .errou(resultado_1_errou));
  LED led_1 (.in(resultado_1_acertou));
  LED led_2 (.in(resultado_1_errou));
endmodule

module navio_1 (
  input  N1_0_in,
  input  N1_1_in,
  input  N1_2_in,
  input  N1_3_in,
  output N1_0_out,
  output N1_1_out,
  output N1_2_out,
  output N1_3_out
);


  assign N1_0_out = N1_0_in;
  assign N1_1_out = N1_1_in;
  assign N1_2_out = N1_2_in;
  assign N1_3_out = N1_3_in;
endmodule

module navio_2 (
  input  N2_0_in,
  input  N2_1_in,
  input  N2_2_in,
  input  N2_3_in,
  output N2_0_out,
  output N2_1_out,
  output N2_2_out,
  output N2_3_out
);


  assign N2_0_out = N2_0_in;
  assign N2_1_out = N2_1_in;
  assign N2_2_out = N2_2_in;
  assign N2_3_out = N2_3_in;
endmodule

module comparador (
  input  N1_0,
  input  N1_1,
  input  N1_2,
  input  N1_3,
  input  alvo_0,
  input  alvo_1,
  input  alvo_2,
  input  alvo_3,
  input  N2_0,
  input  N2_1,
  input  N2_2,
  input  N2_3,
  output S
);

  wire and_1_out, and_2_out, not_1_out, not_2_out, not_3_out, not_4_out, not_5_out, not_6_out, not_7_out,
       not_8_out, xor_1_out, xor_2_out, xor_3_out, xor_4_out, xor_5_out, xor_6_out, xor_7_out, xor_8_out;

  xor xor_1 (xor_1_out, N1_0, alvo_0);
  not not_1 (not_1_out, xor_1_out);
  xor xor_2 (xor_2_out, N1_1, alvo_1);
  not not_2 (not_2_out, xor_2_out);
  xor xor_3 (xor_3_out, N1_2, alvo_2);
  not not_3 (not_3_out, xor_3_out);
  xor xor_4 (xor_4_out, N1_3, alvo_3);
  not not_4 (not_4_out, xor_4_out);
  xor xor_5 (xor_5_out, N2_0, alvo_0);
  not not_5 (not_5_out, xor_5_out);
  xor xor_6 (xor_6_out, N2_1, alvo_1);
  not not_6 (not_6_out, xor_6_out);
  xor xor_7 (xor_7_out, N2_2, alvo_2);
  not not_7 (not_7_out, xor_7_out);
  xor xor_8 (xor_8_out, N2_3, alvo_3);
  not not_8 (not_8_out, xor_8_out);
  and and_1 (and_1_out, not_1_out, not_2_out, not_3_out, not_4_out);
  and and_2 (and_2_out, not_5_out, not_6_out, not_7_out, not_8_out);
  or or_1 (S, and_1_out, and_2_out);
endmodule

module codificador (
  input  linha_1,
  input  linha_0,
  input  coluna_1,
  input  coluna_0,
  output alvo_3,
  output alvo_2,
  output alvo_1,
  output alvo_0
);

  wire and_1_out, and_2_out, and_3_out, and_4_out, and_5_out, and_6_out, and_7_out, and_8_out, and_9_out,
       and_10_out, and_11_out, and_12_out, and_13_out, and_14_out, and_15_out, and_16_out, not_1_out,
       not_2_out, not_3_out, not_4_out;

  not not_1 (not_1_out, linha_1);
  not not_2 (not_2_out, linha_0);
  not not_3 (not_3_out, coluna_1);
  not not_4 (not_4_out, coluna_0);
  and and_1 (and_1_out, not_1_out, coluna_1, coluna_0);
  and and_2 (and_2_out, not_1_out, linha_0);
  and and_3 (and_3_out, linha_1, not_3_out, not_4_out);
  and and_4 (and_4_out, linha_0, not_4_out);
  and and_5 (and_5_out, coluna_1, not_4_out);
  and and_6 (and_6_out, not_1_out, linha_0, coluna_1);
  and and_7 (and_7_out, linha_1, not_2_out, coluna_0);
  and and_8 (and_8_out, linha_1, linha_0, not_4_out);
  and and_9 (and_9_out, not_1_out, not_3_out, coluna_0);
  and and_10 (and_10_out, linha_1, not_3_out, not_4_out);
  and and_11 (and_11_out, linha_0, coluna_1, coluna_0);
  and and_12 (and_12_out, linha_1, not_2_out, coluna_1);
  and and_13 (and_13_out, not_3_out, not_4_out);
  and and_14 (and_14_out, linha_1, not_2_out, not_3_out);
  and and_15 (and_15_out, linha_1, not_4_out);
  and and_16 (and_16_out, linha_1, linha_0, coluna_1);
  or or_1 (alvo_3, and_1_out, and_2_out, and_3_out, and_4_out);
  or or_2 (alvo_2, and_5_out, and_6_out, and_7_out, and_8_out);
  or or_3 (alvo_1, and_9_out, and_10_out, and_11_out, and_12_out);
  or or_4 (alvo_0, and_13_out, and_14_out, and_15_out, and_16_out);
endmodule

module resultado (
  input  comparador,
  input  disparar,
  output acertou,
  output errou
);

  wire not_1_out;

  not not_1 (not_1_out, comparador);
  and and_1 (acertou, comparador, disparar);
  and and_2 (errou, not_1_out, disparar);
endmodule

module Linha (
  input  Linha_0_in,
  input  linha_1_in,
  output linha_0_out,
  output linha_1_out
);


  assign linha_0_out = Linha_0_in;
  assign linha_1_out = linha_1_in;
endmodule

module coluna (
  input  coluna_0_in,
  input  coluna_1_in,
  output coluna_0_out,
  output coluna_1_out
);


  assign coluna_0_out = coluna_0_in;
  assign coluna_1_out = coluna_1_in;
endmodule
