// Logisim project contador.circ as structural Verilog: 1 circuit, main circuit main
module main (
  input  in_1,
  input  in_2,
  output out_3,
  output out_4,
  output out_5,
  output out_6,
  output out_7
);

  wire and_1_out;

  J_K_Flip_Flop #(.trigger("falling")) j_k_ff_1 (
    .J(in_1), .K(in_1), .clk(in_2), .Q(out_7), .reset(and_1_out));  // open: Qn, preset
  J_K_Flip_Flop #(.trigger("falling")) j_k_ff_2 (
    .J(in_1), .K(in_1), .clk(out_7), .Q(out_6), .reset(and_1_out));  // open: Qn, preset
  and and_1 (and_1_out, out_7, out_4);
  J_K_Flip_Flop #(.trigger("falling")) j_k_ff_3 (
    .J(in_1), .K(in_1), .clk(out_6), .Q(out_5), .reset(and_1_out));  // open: Qn, preset
  J_K_Flip_Flop #(.trigger("falling")) j_k_ff_4 (
    .J(in_1), .K(in_1), .clk(out_5), .Q(out_4), .reset(and_1_out));  // open: Qn, preset
  J_K_Flip_Flop #(.trigger("falling")) j_k_ff_5 (
    .J(in_1), .K(in_1), .clk(out_4), .Q(out_3), .reset(and_1_out));  // open: Qn, preset
endmodule
