// Logisim project contador_gray_4bits_ruan.circ as structural Verilog: 9 circuits, main circuit main
module main (
  input  CLK,
  output Q3,
  output Q2,
  output Q1,
  output Q0
);

  wire jq0_1_j0, jq1_1_j1, jq2_1_j2, jq3_1_j3, kq0_1_k0, kq1_1_k1, kq2_1_k2, kq3_1_k3;

  JQ0 jq0_1 (.Q3(Q3), .Q2(Q2), .Q1(Q1), .J0(jq0_1_j0));
  KQ0 kq0_1 (.Q3(Q3), .Q2(Q2), .Q1(Q1), .K0(kq0_1_k0));
  J_K_Flip_Flop j_k_ff_1 (.J(jq0_1_j0), .K(kq0_1_k0), .clk(CLK), .Q(Q0));  // open: Qn, preset, reset
  JQ1 jq1_1 (.Q3(Q3), .Q2(Q2), .Q0(Q0), .J1(jq1_1_j1));
  KQ1 kq1_1 (.Q3(Q3), .Q2(Q2), .Q0(Q0), .K1(kq1_1_k1));
  J_K_Flip_Flop j_k_ff_2 (.J(jq1_1_j1), .K(kq1_1_k1), .clk(CLK), .Q(Q1));  // open: Qn, preset, reset
  JQ2 jq2_1 (.Q3(Q3), .Q1(Q1), .Q0(Q0), .J2(jq2_1_j2));
  KQ2 kq2_1 (.Q3(Q3), .Q1(Q1), .Q0(Q0), .K2(kq2_1_k2));
  J_K_Flip_Flop j_k_ff_3 (.J(jq2_1_j2), .K(kq2_1_k2), .clk(CLK), .Q(Q2));  // open: Qn, preset, reset
  JQ3 jq3_1 (.Q2(Q2), .Q1(Q1), .Q0(Q0), .J3(jq3_1_j3));
  J_K_Flip_Flop j_k_ff_4 (.J(jq3_1_j3), .K(kq3_1_k3), .clk(CLK), .Q(Q3));  // open: Qn, preset, reset
  KQ3 kq3_1 (.Q2(Q2), .Q1(Q1), .Q0(Q0), .K3(kq3_1_k3));
endmodule

module JQ0 (
  input  Q3,
  input  Q2,
  input  Q1,
  output J0
);

  wire and_1_out, and_2_out, and_3_out, and_4_out, not_1_out, not_2_out, not_3_out, not_4_out, not_5_out,
       not_6_out;

  not not_1 (not_1_out, Q3);
  not not_2 (not_2_out, Q2);
  not not_3 (not_3_out, Q1);
  not not_4 (not_4_out, Q3);
  not not_5 (not_5_out, Q2);
  not not_6 (not_6_out, Q1);
  and and_1 (and_1_out, not_1_out, not_2_out, not_3_out);
  and and_2 (and_2_out, not_4_out, Q2, Q1);
  and and_3 (and_3_out, Q3, not_5_out, Q1);
  and and_4 (and_4_out, Q3, Q2, not_6_out);
  or or_1 (J0, and_1_out, and_2_out, and_3_out, and_4_out);
endmodule

module KQ0 (
  input  Q3,
  input  Q2,
  input  Q1,
  output K0
);

  wire and_1_out, and_2_out, and_3_out, and_4_out, not_1_out, not_2_out, not_3_out, not_4_out, not_5_out,
       not_6_out;

  not not_1 (not_1_out, Q3);
  not not_2 (not_2_out, Q2);
  not not_3 (not_3_out, Q3);
  not not_4 (not_4_out, Q1);
  not not_5 (not_5_out, Q2);
  not not_6 (not_6_out, Q1);
  and and_1 (and_1_out, not_1_out, not_2_out, Q1);
  and and_2 (and_2_out, not_3_out, Q2, not_4_out);
  and and_3 (and_3_out, Q3, not_5_out, not_6_out);
  and and_4 (and_4_out, Q3, Q2, Q1);
  or or_1 (K0, and_1_out, and_2_out, and_3_out, and_4_out);
endmodule

module JQ1 (
  input  Q3,
  input  Q2,
  input  Q0,
  output J1
);

  wire and_1_out, and_2_out, not_1_out, not_2_out;

  not not_1 (not_1_out, Q3);
  not not_2 (not_2_out, Q2);
  and and_1 (and_1_out, not_1_out, not_2_out, Q0);
  and and_2 (and_2_out, Q3, Q2, Q0);
  or or_1 (J1, and_1_out, and_2_out);
endmodule

module KQ1 (
  input  Q3,
  input  Q2,
  input  Q0,
  output K1
);

  wire and_1_out, and_2_out, not_1_out, not_2_out;

  not not_1 (not_1_out, Q3);
  not not_2 (not_2_out, Q2);
  and and_1 (and_1_out, not_1_out, Q2, Q0);
  and and_2 (and_2_out, Q3, not_2_out, Q0);
  or or_1 (K1, and_1_out, and_2_out);
endmodule

module JQ2 (
  input  Q3,
  input  Q1,
  input  Q0,
  output J2
);

  wire not_1_out, not_2_out;

  not not_1 (not_1_out, Q3);
  and and_1 (J2, not_1_out, Q1, not_2_out);
  not not_2 (not_2_out, Q0);
endmodule

module KQ2 (
  input  Q3,
  input  Q1,
  input  Q0,
  output K2
);

  wire not_1_out;

  not not_1 (not_1_out, Q0);
  and and_1 (K2, Q3, Q1, not_1_out);
endmodule

module JQ3 (
  input  Q2,
  input  Q1,
  input  Q0,
  output J3
);

  wire not_1_out, not_2_out;

  not not_1 (not_1_out, Q1);
  not not_2 (not_2_out, Q0);
  and and_1 (J3, Q2, not_1_out, not_2_out);
endmodule

module KQ3 (
  input  Q2,
  input  Q1,
  input  Q0,
  output K3
);

  wire not_1_out, not_2_out, not_3_out;

  not not_1 (not_1_out, Q2);
  not not_2 (not_2_out, Q1);
  and and_1 (K3, not_1_out, not_2_out, not_3_out);
  not not_3 (not_3_out, Q0);
endmodule
