// Logisim project contador_grey_4bits.circ as structural Verilog: 1 circuit, main circuit main
module main (
  input  CLK,
  output Q3,
  output Q2,
  output Q1,
  output Q0
);

  J_K_Flip_Flop j_k_ff_1 (.clk(CLK), .Q(Q0));  // open: J, K, Qn, preset, reset
  J_K_Flip_Flop j_k_ff_2 (.clk(CLK), .Q(Q1));  // open: J, K, Qn, preset, reset
  J_K_Flip_Flop j_k_ff_3 (.clk(CLK), .Q(Q2));  // open: J, K, Qn, preset, reset
  J_K_Flip_Flop j_k_ff_4 (.clk(CLK), .Q(Q3));  // open: J, K, Qn, preset, reset
endmodule
