// Logisim project contadorgrey.circ as structural Verilog: 2 circuits, main circuit main
module main (
  input  CLK,
  output Q3,
  output Q2,
  output Q1,
  output Q0
);

  J_K_Flip_Flop j_k_ff_1 (.clk(CLK), .Q(Q0));  // open: J, K, Qn, preset, reset
  J_K_Flip_Flop j_k_ff_2 (.clk(CLK), .Q(Q1));  // open: J, K, Qn, preset, reset
  J_K_Flip_Flop j_k_ff_3 (.clk(CLK), .Q(Q2));  // open: J, K, Qn, preset, reset
  J_K_Flip_Flop j_k_ff_4 (.clk(CLK), .Q(Q3));  // open: J, K, Qn, preset, reset
endmodule

module contador_grey (
  input  in_1,
  output out_2,
  output out_3,
  output out_4
);

  wire and_1_out, and_2_out, and_3_out, and_4_out, j_k_ff_1_qn, j_k_ff_2_qn, j_k_ff_3_qn, not_1_out,
       xor_1_out, xor_2_out;

  xor xor_1 (xor_1_out, out_2, out_3);
  xor xor_2 (xor_2_out, out_2, out_3);
  not not_1 (not_1_out, xor_1_out);
  J_K_Flip_Flop j_k_ff_1 (
    .J(not_1_out), .K(xor_2_out), .clk(in_1), .Q(out_4), .Qn(j_k_ff_1_qn));  // open: preset, reset
  and and_1 (and_1_out, out_4, j_k_ff_3_qn);
  and and_2 (and_2_out, out_4, out_2);
  J_K_Flip_Flop j_k_ff_2 (
    .J(and_1_out), .K(and_2_out), .clk(in_1), .Q(out_3), .Qn(j_k_ff_2_qn));  // open: preset, reset
  and and_3 (and_3_out, out_3, j_k_ff_1_qn);
  J_K_Flip_Flop j_k_ff_3 (
    .J(and_3_out), .K(and_4_out), .clk(in_1), .Q(out_2), .Qn(j_k_ff_3_qn));  // open: preset, reset
  and and_4 (and_4_out, j_k_ff_2_qn, j_k_ff_1_qn);
endmodule
