// Logisim project registradores.circ as structural Verilog: 1 circuit, main circuit main
module main (
  input  d3,
  input  d2,
  input  d1,
  input  d0,
  input  d5,
  input  d4,
  input  t,
  input  in_8,
  input  in_9,
  input  in_10,
  input  write,
  input  read,
  input  in_13,
  input  in_14,
  input  in_15,
  input  in_16,
  output out_17,
  output q1,
  output q0,
  output q5,
  output q2,
  output q4,
  output q3,
  output out_24,
  output out_25,
  output out_26,
  output out_27,
  output out_28,
  output out_29,
  output out_30,
  output out_31
);

  wire d_ff_2_q, d_ff_4_q, d_ff_5_q, d_ff_7_q, d_ff_9_q, d_ff_10_q;

  D_Flip_Flop d_ff_1 (.D(in_14), .clk(in_16), .Q(out_31));  // open: Qn, preset, reset
  D_Flip_Flop d_ff_2 (.D(d5), .clk(write), .Q(d_ff_2_q));  // open: Qn, preset, reset
  and and_1 (q5, d_ff_2_q, read);
  D_Flip_Flop d_ff_3 (.D(out_31), .clk(in_16), .Q(out_27));  // open: Qn, preset, reset
  D_Flip_Flop d_ff_4 (.D(d4), .clk(write), .Q(d_ff_4_q));  // open: Qn, preset, reset
  and and_2 (q4, d_ff_4_q, read);
  D_Flip_Flop d_ff_5 (.D(d3), .clk(write), .Q(d_ff_5_q));  // open: Qn, preset, reset
  D_Flip_Flop d_ff_6 (.D(out_27), .clk(in_16), .Q(out_30));  // open: Qn, preset, reset
  and and_3 (q3, d_ff_5_q, read);
  D_Flip_Flop d_ff_7 (.D(d2), .clk(write), .Q(d_ff_7_q));  // open: Qn, preset, reset
  D_Flip_Flop d_ff_8 (.D(out_30), .clk(in_16), .Q(out_29));  // open: Qn, preset, reset
  and and_4 (q2, d_ff_7_q, read);
  D_Flip_Flop d_ff_9 (.D(d1), .clk(write), .Q(d_ff_9_q));  // open: Qn, preset, reset
  D_Flip_Flop d_ff_10 (.D(d0), .clk(write), .Q(d_ff_10_q));  // open: Qn, preset, reset
  and and_5 (q1, d_ff_9_q, read);
  and and_6 (q0, d_ff_10_q, read);
  D_Flip_Flop d_ff_11 (.D(out_24), .clk(in_15), .Q(out_28));  // open: Qn, preset, reset
  Register #(.width(1)) register_1 (.D(t), .en(in_8), .clk(in_9), .Q(out_17), .clr(in_10));
  D_Flip_Flop d_ff_12 (.D(out_26), .clk(in_15), .Q(out_24));  // open: Qn, preset, reset
  D_Flip_Flop d_ff_13 (.D(out_25), .clk(in_15), .Q(out_26));  // open: Qn, preset, reset
  D_Flip_Flop d_ff_14 (.D(in_13), .clk(in_15), .Q(out_25));  // open: Qn, preset, reset
endmodule
