// Logisim project karno_cod_decod.circ as structural Verilog
module decolder (
  input  in_1,
  input  in_2,
  input  in_3,
  input  d,
  output A,
  output B,
  output C,
  output out_8
);

  wire and_1_out, and_2_out, and_3_out, and_4_out, and_5_out, and_6_out, and_7_out, and_8_out, and_9_out,
       and_10_out, and_11_out, and_12_out, and_13_out, and_14_out, and_15_out, and_16_out, not_1_out,
       not_2_out, not_3_out, not_4_out;

  not not_1 (not_1_out, in_1);
  not not_2 (not_2_out, in_2);
  not not_3 (not_3_out, in_3);
  not not_4 (not_4_out, d);
  and and_1 (and_1_out, not_1_out, not_2_out, not_3_out);
  and and_2 (and_2_out, not_2_out, d);
  and and_3 (and_3_out, not_1_out, in_2, in_3, not_4_out);
  and and_4 (and_4_out, in_1, in_2, not_3_out, not_4_out);
  and and_5 (and_5_out, in_1, in_3, d);
  and and_6 (and_6_out, not_1_out, not_2_out, in_3);
  and and_7 (and_7_out, not_1_out, not_3_out, d);
  and and_8 (and_8_out, in_1, not_2_out, not_3_out);
  and and_9 (and_9_out, in_1, in_2, not_4_out);
  and and_10 (and_10_out, not_1_out, in_3, d);
  and and_11 (and_11_out, in_2, d);
  and and_12 (and_12_out, in_2, in_3);
  and and_13 (and_13_out, not_1_out, not_2_out, d);
  and and_14 (and_14_out, not_2_out, not_3_out, not_4_out);
  and and_15 (and_15_out, not_1_out, in_2, not_4_out);
  and and_16 (and_16_out, in_2, not_3_out, d);
  or or_1 (A, and_1_out, and_2_out, and_3_out, and_4_out, and_5_out);
  or or_2 (B, and_6_out, and_7_out, and_8_out, and_9_out);
  or or_3 (C, and_10_out, and_11_out, and_12_out);
  or or_4 (out_8, and_13_out, and_14_out, and_15_out, and_16_out);
endmodule

module coder (
  input  A,
  input  in_2,
  input  C,
  input  in_4,
  output out_5,
  output b,
  output out_7,
  output d
);

  wire and_1_out, and_2_out, and_3_out, and_4_out, and_5_out, and_6_out, and_7_out, and_8_out, and_9_out,
       and_10_out, and_11_out, and_12_out, and_13_out, and_14_out, and_15_out, and_16_out, and_17_out,
       and_18_out, not_1_out, not_2_out, not_3_out, not_4_out;

  not not_1 (not_1_out, A);
  not not_2 (not_2_out, in_2);
  not not_3 (not_3_out, C);
  not not_4 (not_4_out, in_4);
  and and_1 (and_1_out, not_2_out, not_3_out, not_4_out);
  and and_2 (and_2_out, not_1_out, not_2_out, C, in_4);
  and and_3 (and_3_out, not_1_out, in_2, not_3_out, in_4);
  and and_4 (and_4_out, in_2, C, not_4_out);
  and and_5 (and_5_out, A, not_4_out);
  and and_6 (and_6_out, not_1_out, not_2_out, in_4);
  and and_7 (and_7_out, not_1_out, C);
  and and_8 (and_8_out, not_2_out, C);
  and and_9 (and_9_out, C, not_4_out);
  and and_10 (and_10_out, not_1_out, not_4_out);
  and and_11 (and_11_out, not_2_out, not_4_out);
  and and_12 (and_12_out, A, C, in_4);
  and and_13 (and_13_out, not_1_out, not_2_out, C);
  and and_14 (and_14_out, not_1_out, C, in_4);
  and and_15 (and_15_out, A, not_2_out, not_4_out);
  and and_16 (and_16_out, A, not_3_out, not_4_out);
  and and_17 (and_17_out, A, in_2, not_3_out);
  and and_18 (and_18_out, in_2, C, in_4);
  or or_1 (out_5, and_1_out, and_2_out, and_3_out, and_4_out, and_5_out);
  or or_2 (b, and_6_out, and_7_out, and_8_out, and_9_out);
  or or_3 (out_7, and_10_out, and_11_out, and_12_out);
  or or_4 (d, and_13_out, and_14_out, and_15_out, and_16_out, and_17_out, and_18_out);
endmodule
